# Fritzing sketch 02_harici_led_yakma (saved by Fritzing 0.9.2b)
breadboards: 1

parts:
  Eleman1 = BluePill
  LED1 = LED - 5mm [color="Green (555nm)" package="5 mm [THT]"]

nets:
  N1: Eleman1.GND2, LED1.cathode
  N2: Eleman1.B13, LED1.anode
