# Fritzing sketch 03_buton_ile_led_yakma (saved by Fritzing 0.9.2b)
breadboards: 1

parts:
  Eleman1 = BluePill
  LED1 = LED - 5mm [color="Red (633nm)" package="5 mm [THT]"]
  S1 = Pushbutton [package="[SMD]"]
  R1 = Resistor [tolerance=±5% resistance=220 package=THT]

nets:
  N1: Eleman1.A6, S1.Pin_1, S1.Pin_2, R1.Pin_0
  N2: Eleman1.A7, LED1.anode
  N3: Eleman1.3V3, S1.Pin_3, S1.Pin_4
  N4: Eleman1.GND, LED1.cathode, R1.Pin_1
