# Fritzing sketch 05_external_interrupt (saved by Fritzing 0.9.2b)
breadboards: 1

parts:
  Eleman1 = BluePill
  S1 = Pushbutton [package="[THT]"]
  R1 = Resistor [tolerance=±5% resistance=10 package=THT]

nets:
  N1: Eleman1.3V3, S1.Pin_3, S1.Pin_4
  N2: Eleman1.GND, R1.Pin_1
  N3: Eleman1.B12, S1.Pin_1, S1.Pin_2, R1.Pin_0
