# Fritzing sketch 09_adc_interrupt (saved by Fritzing 0.9.2b)
breadboards: 1

parts:
  Eleman1 = BluePill
  R1 = Rotary Potentiometer (Small) [maximum_resistance=100kΩ package=THT]

nets:
  N1: Eleman1.A0, R1.wiper
  N2: Eleman1.3V3, R1.leg1
  N3: Eleman1.GND2, R1.leg2
